// Logisim project cpu-shell.circ as structural Verilog: 9 circuits, main circuit main
module main (
);

  Call_Stack call_stack_1 ();  // open: Push_Pop, CLK, En, AddrOut
  Control_Unit control_unit_1 ();  // open: in_1
  PC pc_1 ();  // open: in_1, out_2
  Instruction_Memory instruction_memory_1 ();  // open: in_1, out_2
  Registers registers_1 ();  // open: R1, R2, W, D, CLK, En, R1_2, R2_2
  ALU alu_1 ();  // open: in_1, in_2, in_3, out_4
  Flags flags_1 ();  // open: Set_flag, CLK
  Data_Memory data_memory_1 ();  // open: Data, Addr, R_W, En, out_5
endmodule

module PC (
  input  [9:0] in_1,
  output [9:0] out_2
);
endmodule

module Instruction_Memory (
  input  [9:0] in_1,
  output [15:0] out_2
);
endmodule

module Registers (
  input  [2:0] R1,
  input  [2:0] R2,
  input  [3:0] W,
  input  [7:0] D,
  input  CLK,
  input  En,
  output [7:0] R1_2,
  output [7:0] R2_2
);

  // AND_Gate and_1 has open pins: out=R1_2
  // AND_Gate and_2 has open pins: out=R2_2
endmodule

module ALU (
  input  [2:0] in_1,
  input  [7:0] in_2,
  input  [7:0] in_3,
  output [7:0] out_4
);
endmodule

module Data_Memory (
  input  [7:0] Data,
  input  [7:0] Addr,
  input  R_W,
  input  En,
  output [7:0] out_5
);
endmodule

module Call_Stack (
  input  Push_Pop,
  input  CLK,
  input  En,
  output [9:0] AddrOut
);
endmodule

module Flags (
  input  Set_flag,
  input  CLK
);
endmodule

module Control_Unit (
  input  [3:0] in_1
);
endmodule
