// Logisim project early-register-layout.circ as structural Verilog: 1 circuit, main circuit main
module main (
);

  Register R1 ();  // open: D, en, Q, clk, clr
  Register R4 ();  // open: D, en, Q, clk, clr
  Register R0 ();  // open: D, en, Q, clk, clr
  Register R2 ();  // open: D, en, Q, clk, clr
  Register R5 ();  // open: D, en, Q, clk, clr
  Register R7 ();  // open: D, en, Q, clk, clr
  Register R3 ();  // open: D, en, Q, clk, clr
  Register R6 ();  // open: D, en, Q, clk, clr
  Multiplexer #(.select(5), .width(8)) multiplexer_1 ();  // open: in0, in1, in2, in3, in4, in5, in6, in7, in8, in9, in10, in11, in12, in13, in14, in15, in16, in17, in18, in19, in20, in21, in22, in23, in24, in25, in26, in27, in28, in29, in30, in31, out, sel, en
  Counter counter_1 ();  // open: load, D, count, Q, carry, clk, clr
  ROM #(.dataWidth(16)) rom_1 ();  // open: addr, data, sel
endmodule
