// Logisim project cpu.circ as structural Verilog: 28 circuits, main circuit main
module main (
  input  CKL_IN,
  input  CLK_EN,
  input  MANUAL_CLK,
  input  Halt,
  output CLK_OUT
);

  wire and_1_out, and_2_out, not_1_out, not_2_out, or_1_out;

  Call_Stack call_stack_1 ();  // open: Push_Pop, CLK, En, AddrOut
  Control_Unit control_unit_1 ();  // open: OPCODE, REG_WRITE, MEM_WRITE, FLAG_WRITE, PC_LOAD, PC_EN, WB_SEL, ZERO, CARRY, NEGATIVE, FLAG_SEL
  PC pc_1 ();  // open: CLK, RESET, PC_EN, PC_LOAD, JUMP_ADDR, OUT
  Instruction_Memory instruction_memory_1 ();  // open: INSTR, ADDR
  Registers registers_1 ();  // open: READ_A, READ_B, WRITE_ADDR, D, CLK, WRITE_En, A_OUT, B_OUT, RESET, R7
  ALU alu_1 ();  // open: OPCODE, A, B, Y, CARRY, ZERO, NEGATIVE
  Flags flags_1 ();  // open: RESET, CLK, FLAG_WRITE, ZERO_IN, CARRY_IN, NEGATIVE_IN, ZERO_OUT, CARRY_OUT, NEGATIVE_OUT
  Data_Memory data_memory_1 ();  // open: Data, Addr, R_W, READ_DATA, CLK, RESET
  // NOT_Gate not_1 has open pins: in=open, out=not_1_out
  not not_2 (not_2_out, CLK_EN);
  and and_1 (and_1_out, CKL_IN, CLK_EN);
  and and_2 (and_2_out, not_2_out, MANUAL_CLK);
  or or_1 (or_1_out, and_1_out, and_2_out);
  and and_3 (CLK_OUT, or_1_out, not_1_out);
endmodule

module PC (
  input  [7:0] JUMP_ADDR,
  input  PC_EN,
  input  PC_LOAD,
  input  CLK,
  input  RESET,
  output [7:0] OUT
);

  wire [7:0] mux_2_to_1_8bit_1_y, n8bitadder_1_pc_plus_1, register_1_dout;

  Register register_1 (
    .Din(mux_2_to_1_8bit_1_y), .Write(PC_EN), .CLK(CLK), .OUT_EN(1'b1), .Reset(RESET),
    .Dout(register_1_dout), .Store(OUT));
  _8BITADDER u_8bitadder_1 (
    .PC0(register_1_dout[0]), .PC1(register_1_dout[1]), .PC2(register_1_dout[2]), .PC3(register_1_dout[3]),
    .PC4(register_1_dout[4]), .PC5(register_1_dout[5]), .PC6(register_1_dout[6]), .PC7(register_1_dout[7]),
    .PC_PLUS_1(n8bitadder_1_pc_plus_1));
  MUX_2_TO_1_8BIT mux_2_to_1_8bit_1 (.A(JUMP_ADDR), .SEL(PC_LOAD), .B(n8bitadder_1_pc_plus_1), .Y(mux_2_to_1_8bit_1_y));
endmodule

module Instruction_Memory (
  input  [7:0] ADDR,
  output [15:0] INSTR
);

  Multiplexer #(.select(4), .width(16)) multiplexer_1 (
    .in0(16'h6710), .in1(16'h6105), .in2(16'h6203), .in3({16{1'b1}}), .in4({16{1'b1}}), .in5({16{1'b1}}),
    .in6({16{1'b1}}), .in7({16{1'b1}}), .in8({16{1'b1}}), .in9({16{1'b1}}), .in10({16{1'b1}}),
    .in11({16{1'b1}}), .in12({16{1'b1}}), .in13({16{1'b1}}), .in14({16{1'b1}}), .in15({16{1'b1}}),
    .out(INSTR), .sel(ADDR[3:0]), .en(1'b1));
endmodule

module Registers (
  input  [7:0] D,
  input  [3:0] READ_A,
  input  [3:0] WRITE_ADDR,
  input  CLK,
  input  WRITE_En,
  input  RESET,
  input  [3:0] READ_B,
  output [7:0] A_OUT,
  output [7:0] B_OUT,
  output [7:0] R7
);

  wire and_1_out, and_2_out, and_3_out, and_4_out, and_5_out, and_6_out, and_7_out, decoder_1_out1,
       decoder_1_out2, decoder_1_out3, decoder_1_out4, decoder_1_out5, decoder_1_out6, decoder_1_out7;
  wire [7:0] register_1_store, register_2_store, register_3_store, register_4_store, register_5_store,
       register_6_store;

  Decoder_part #(.select(4)) decoder_1 (
    .out1(decoder_1_out1), .out2(decoder_1_out2), .out3(decoder_1_out3), .out4(decoder_1_out4),
    .out5(decoder_1_out5), .out6(decoder_1_out6), .out7(decoder_1_out7), .sel(WRITE_ADDR), .en(1'b1));  // open: out0, out8, out9, out10, out11, out12, out13, out14, out15
  and and_1 (and_1_out, decoder_1_out1, WRITE_En);
  and and_2 (and_2_out, decoder_1_out2, WRITE_En);
  and and_3 (and_3_out, decoder_1_out3, WRITE_En);
  and and_4 (and_4_out, decoder_1_out4, WRITE_En);
  and and_5 (and_5_out, decoder_1_out5, WRITE_En);
  and and_6 (and_6_out, decoder_1_out6, WRITE_En);
  and and_7 (and_7_out, decoder_1_out7, WRITE_En);
  Register register_1 (
    .Din(D), .Write(and_1_out), .CLK(CLK), .OUT_EN(1'b1), .Reset(RESET), .Store(register_1_store));  // open: Dout
  Register register_2 (
    .Din(D), .Write(and_2_out), .CLK(CLK), .OUT_EN(1'b1), .Reset(RESET), .Store(register_2_store));  // open: Dout
  Register register_3 (
    .Din(D), .Write(and_3_out), .CLK(CLK), .OUT_EN(1'b1), .Reset(RESET), .Store(register_3_store));  // open: Dout
  Register register_4 (
    .Din(D), .Write(and_4_out), .CLK(CLK), .OUT_EN(1'b1), .Reset(RESET), .Store(register_4_store));  // open: Dout
  Register register_5 (
    .Din(D), .Write(and_5_out), .CLK(CLK), .OUT_EN(1'b1), .Reset(RESET), .Store(register_5_store));  // open: Dout
  Register register_6 (
    .Din(D), .Write(and_6_out), .CLK(CLK), .OUT_EN(1'b1), .Reset(RESET), .Store(register_6_store));  // open: Dout
  Register register_7 (.Din(D), .Write(and_7_out), .CLK(CLK), .OUT_EN(1'b1), .Reset(RESET), .Store(R7));  // open: Dout
  Multiplexer #(.select(4), .width(8)) multiplexer_1 (
    .in0({8{1'b0}}), .in1(register_1_store), .in2(register_2_store), .in3(register_3_store),
    .in4(register_4_store), .in5(register_5_store), .in6(register_6_store), .in7(R7), .out(A_OUT),
    .sel(READ_A), .en(1'b1));  // open: in8, in9, in10, in11, in12, in13, in14, in15
  Multiplexer #(.select(4), .width(8)) multiplexer_2 (
    .in0({8{1'b0}}), .in1(register_1_store), .in2(register_2_store), .in3(register_3_store),
    .in4(register_4_store), .in5(register_5_store), .in6(register_6_store), .in7(R7), .out(B_OUT),
    .sel(READ_B), .en(1'b1));  // open: in8, in9, in10, in11, in12, in13, in14, in15
endmodule

module ALU (
  input  [7:0] A,
  input  [7:0] B,
  input  [3:0] OPCODE,
  output [7:0] Y,
  output ZERO,
  output CARRY,
  output NEGATIVE
);

  wire rightshift_1_rshcarry;
  wire [7:0] aludecoder_1_p2, aludecoder_1_p3, aludecoder_1_p4, aludecoder_1_p5, aludecoder_1_p6,
       aludecoder_1_p7, aludecoder_1_p8, and_1_out, and_3_out, and_4_out, and_5_out, and_6_out,
       bitwiseand_1_y, bitwisenor_1_y, n8bitadd_sub_1_y, or_1_out, or_2_out, or_3_out, or_4_out,
       rightshift_1_rsh;

  // ALUDECODER aludecoder_1: pin names not known; wires that end beside it: OPCODE, aludecoder_1_p2, aludecoder_1_p3, aludecoder_1_p4, aludecoder_1_p5, aludecoder_1_p6, aludecoder_1_p7, aludecoder_1_p8
  assign or_1_out = aludecoder_1_p2 | aludecoder_1_p3 | aludecoder_1_p6 | aludecoder_1_p7;  // OR_Gate or_1, 8 bits wide
  assign or_2_out = aludecoder_1_p2 | aludecoder_1_p3;  // OR_Gate or_2, 8 bits wide
  assign or_3_out = aludecoder_1_p3 | aludecoder_1_p7;  // OR_Gate or_3, 8 bits wide
  assign or_4_out = aludecoder_1_p6 | aludecoder_1_p7;  // OR_Gate or_4, 8 bits wide
  assign and_1_out = B & or_2_out;  // AND_Gate and_1, 8 bits wide
  assign and_1_out = or_4_out & 8'h1;  // AND_Gate and_2, 8 bits wide
  _8BITADD_SUB u_8bitadd_sub_1 (.ADD_SUB(or_3_out[0]), .A(A), .B(and_1_out), .Y(n8bitadd_sub_1_y), .Cout(CARRY));
  RIGHTSHIFT rightshift_1 (.IN(A), .RSHCARRY(rightshift_1_rshcarry), .RSH(rightshift_1_rsh));  // open: in_2
  BITWISENOR bitwisenor_1 (.A(A), .B(B), .Y(bitwisenor_1_y));
  BITWISEAND bitwiseand_1 (.A(A), .B(B), .Y(bitwiseand_1_y));
  assign and_3_out = or_1_out & n8bitadd_sub_1_y;  // AND_Gate and_3, 8 bits wide
  assign and_4_out = rightshift_1_rsh & aludecoder_1_p8;  // AND_Gate and_4, 8 bits wide
  assign and_5_out = aludecoder_1_p4 & bitwisenor_1_y;  // AND_Gate and_5, 8 bits wide
  assign and_6_out = aludecoder_1_p5 & bitwiseand_1_y;  // AND_Gate and_6, 8 bits wide
  assign Y = and_3_out | and_5_out | and_6_out | and_4_out;  // OR_Gate or_5, 8 bits wide
  // Pins of 1 and 8 bits meet at or_3_out
endmodule

module Data_Memory (
  input  [7:0] Addr,
  input  CLK,
  input  R_W,
  input  RESET,
  input  [7:0] Data,
  output [7:0] READ_DATA
);

  wire and_1_out, and_2_out, and_3_out, and_4_out, and_5_out, and_6_out, and_7_out, and_8_out, and_9_out,
       and_10_out, and_11_out, and_12_out, and_13_out, and_14_out, and_15_out, and_16_out, decoder_1_out0,
       decoder_1_out1, decoder_1_out2, decoder_1_out3, decoder_1_out4, decoder_1_out5, decoder_1_out6,
       decoder_1_out7, decoder_1_out8, decoder_1_out9, decoder_1_out10, decoder_1_out11, decoder_1_out12,
       decoder_1_out13, decoder_1_out14, decoder_1_out15, not_1_out;
  wire [7:0] register_1_store, register_2_store, register_3_store, register_4_store, register_5_store,
       register_6_store, register_7_store, register_8_store, register_9_store, register_10_store,
       register_11_store, register_12_store, register_13_store, register_14_store, register_15_store,
       register_16_store;

  Decoder_part #(.select(4)) decoder_1 (
    .out0(decoder_1_out0), .out1(decoder_1_out1), .out2(decoder_1_out2), .out3(decoder_1_out3),
    .out4(decoder_1_out4), .out5(decoder_1_out5), .out6(decoder_1_out6), .out7(decoder_1_out7),
    .out8(decoder_1_out8), .out9(decoder_1_out9), .out10(decoder_1_out10), .out11(decoder_1_out11),
    .out12(decoder_1_out12), .out13(decoder_1_out13), .out14(decoder_1_out14), .out15(decoder_1_out15),
    .sel(Addr[3:0]), .en(1'b1));
  not not_1 (not_1_out, R_W);
  and and_1 (and_1_out, decoder_1_out0, R_W);
  and and_2 (and_2_out, decoder_1_out1, R_W);
  and and_3 (and_3_out, decoder_1_out2, R_W);
  and and_4 (and_4_out, decoder_1_out3, R_W);
  and and_5 (and_5_out, decoder_1_out4, R_W);
  and and_6 (and_6_out, decoder_1_out5, R_W);
  and and_7 (and_7_out, decoder_1_out6, R_W);
  and and_8 (and_8_out, decoder_1_out7, R_W);
  and and_9 (and_9_out, decoder_1_out8, R_W);
  and and_10 (and_10_out, decoder_1_out9, R_W);
  and and_11 (and_11_out, decoder_1_out10, R_W);
  and and_12 (and_12_out, decoder_1_out11, R_W);
  and and_13 (and_13_out, decoder_1_out12, R_W);
  and and_14 (and_14_out, decoder_1_out13, R_W);
  and and_15 (and_15_out, decoder_1_out14, R_W);
  and and_16 (and_16_out, decoder_1_out15, R_W);
  Register register_1 (
    .Din(Data), .Write(and_1_out), .CLK(CLK), .OUT_EN(1'b1), .Reset(RESET), .Store(register_1_store));  // open: Dout
  Register register_2 (
    .Din(Data), .Write(and_2_out), .CLK(CLK), .OUT_EN(1'b1), .Reset(RESET), .Store(register_2_store));  // open: Dout
  Register register_3 (
    .Din(Data), .Write(and_3_out), .CLK(CLK), .OUT_EN(1'b1), .Reset(RESET), .Store(register_3_store));  // open: Dout
  Register register_4 (
    .Din(Data), .Write(and_4_out), .CLK(CLK), .OUT_EN(1'b1), .Reset(RESET), .Store(register_4_store));  // open: Dout
  Register register_5 (
    .Din(Data), .Write(and_5_out), .CLK(CLK), .OUT_EN(1'b1), .Reset(RESET), .Store(register_5_store));  // open: Dout
  Register register_6 (
    .Din(Data), .Write(and_6_out), .CLK(CLK), .OUT_EN(1'b1), .Reset(RESET), .Store(register_6_store));  // open: Dout
  Register register_7 (
    .Din(Data), .Write(and_7_out), .CLK(CLK), .OUT_EN(1'b1), .Reset(RESET), .Store(register_7_store));  // open: Dout
  Register register_8 (
    .Din(Data), .Write(and_8_out), .CLK(CLK), .OUT_EN(1'b1), .Reset(RESET), .Store(register_8_store));  // open: Dout
  Register register_9 (
    .Din(Data), .Write(and_9_out), .CLK(CLK), .OUT_EN(1'b1), .Reset(RESET), .Store(register_9_store));  // open: Dout
  Register register_10 (
    .Din(Data), .Write(and_10_out), .CLK(CLK), .OUT_EN(1'b1), .Reset(RESET), .Store(register_10_store));  // open: Dout
  Register register_11 (
    .Din(Data), .Write(and_11_out), .CLK(CLK), .OUT_EN(1'b1), .Reset(RESET), .Store(register_11_store));  // open: Dout
  Register register_12 (
    .Din(Data), .Write(and_12_out), .CLK(CLK), .OUT_EN(1'b1), .Reset(RESET), .Store(register_12_store));  // open: Dout
  Register register_13 (
    .Din(Data), .Write(and_13_out), .CLK(CLK), .OUT_EN(1'b1), .Reset(RESET), .Store(register_13_store));  // open: Dout
  Register register_14 (
    .Din(Data), .Write(and_14_out), .CLK(CLK), .OUT_EN(1'b1), .Reset(RESET), .Store(register_14_store));  // open: Dout
  Register register_15 (
    .Din(Data), .Write(and_15_out), .CLK(CLK), .OUT_EN(1'b1), .Reset(RESET), .Store(register_15_store));  // open: Dout
  Register register_16 (
    .Din(Data), .Write(and_16_out), .CLK(CLK), .OUT_EN(1'b1), .Reset(RESET), .Store(register_16_store));  // open: Dout
  Multiplexer #(.select(4), .width(8)) multiplexer_1 (
    .in0(register_1_store), .in1(register_2_store), .in2(register_3_store), .in3(register_4_store),
    .in4(register_5_store), .in5(register_6_store), .in6(register_7_store), .in7(register_8_store),
    .in8(register_9_store), .in9(register_10_store), .in10(register_11_store), .in11(register_12_store),
    .in12(register_13_store), .in13(register_14_store), .in14(register_15_store), .in15(register_16_store),
    .out(READ_DATA), .sel(Addr[3:0]), .en(not_1_out));
endmodule

module Call_Stack (
  input  Push_Pop,
  input  CLK,
  input  En,
  output [9:0] AddrOut
);
endmodule

module Flags (
  input  ZERO_IN,
  input  CARRY_IN,
  input  NEGATIVE_IN,
  input  FLAG_WRITE,
  input  CLK,
  input  RESET,
  output ZERO_OUT,
  output CARRY_OUT,
  output NEGATIVE_OUT
);

  Memory_cell memory_cell_1 (
    .Write_EN(FLAG_WRITE), .Din(ZERO_IN), .CLK(CLK), .OUT_EN(1'b1), .RESET(RESET), .Stored_DATA(ZERO_OUT));  // open: Dout
  Memory_cell memory_cell_2 (
    .Write_EN(FLAG_WRITE), .Din(CARRY_IN), .CLK(CLK), .OUT_EN(1'b1), .RESET(RESET), .Stored_DATA(CARRY_OUT));  // open: Dout
  Memory_cell memory_cell_3 (
    .Write_EN(FLAG_WRITE), .Din(NEGATIVE_IN), .CLK(CLK), .OUT_EN(1'b1), .RESET(RESET),
    .Stored_DATA(NEGATIVE_OUT));  // open: Dout
endmodule

module Control_Unit (
  input  [3:0] OPCODE,
  input  ZERO,
  input  CARRY,
  input  NEGATIVE,
  input  [1:0] FLAG_SEL,
  output REG_WRITE,
  output MEM_WRITE,
  output FLAG_WRITE,
  output PC_LOAD,
  output PC_EN,
  output [1:0] WB_SEL
);

  wire and_1_out, decoder_1_out1, decoder_1_out2, decoder_1_out3, decoder_1_out5, decoder_1_out6,
       decoder_1_out8, decoder_1_out9, decoder_1_out10, decoder_1_out11, decoder_1_out12, decoder_1_out14,
       decoder_1_out15, multiplexer_1_out, or_1_out;

  Decoder_part #(.select(4)) decoder_1 (
    .out1(decoder_1_out1), .out2(decoder_1_out2), .out3(decoder_1_out3), .out5(decoder_1_out5),
    .out6(decoder_1_out6), .out8(decoder_1_out8), .out9(decoder_1_out9), .out10(decoder_1_out10),
    .out11(decoder_1_out11), .out12(decoder_1_out12), .out13(MEM_WRITE), .out14(decoder_1_out14),
    .out15(decoder_1_out15), .sel(OPCODE), .en(1'b1));  // open: out0, out4, out7
  Multiplexer #(.select(2)) multiplexer_1 (
    .in0(ZERO), .in1(CARRY), .in2(NEGATIVE), .out(multiplexer_1_out), .sel(FLAG_SEL), .en(1'b1));  // open: in3
  and and_1 (and_1_out, decoder_1_out15, multiplexer_1_out);
  or or_1 (or_1_out, decoder_1_out2, decoder_1_out3, decoder_1_out5, decoder_1_out6, decoder_1_out8, decoder_1_out9, decoder_1_out10);
  or or_2 (PC_LOAD, decoder_1_out14, and_1_out);
  or or_3 (FLAG_WRITE, or_1_out, decoder_1_out11, decoder_1_out12);
  not not_1 (PC_EN, decoder_1_out1);

  assign REG_WRITE = FLAG_WRITE;
endmodule

module CLK (
  input  CKL_IN,
  input  CLK_EN,
  input  MANUAL_CLK,
  input  Halt,
  output CLK_OUT
);

  wire and_1_out, and_2_out, not_1_out, not_2_out, or_1_out;

  not not_1 (not_1_out, Halt);
  not not_2 (not_2_out, CLK_EN);
  and and_1 (and_1_out, CKL_IN, CLK_EN);
  and and_2 (and_2_out, not_2_out, MANUAL_CLK);
  or or_1 (or_1_out, and_1_out, and_2_out);
  and and_3 (CLK_OUT, or_1_out, not_1_out);
endmodule

module Memory_cell (
  input  Write_EN,
  input  Din,
  input  CLK,
  input  OUT_EN,
  input  RESET,
  output Dout,
  output Stored_DATA
);

  wire and_1_out, and_2_out, not_1_out, or_1_out;

  not not_1 (not_1_out, Write_EN);
  and and_1 (and_1_out, Stored_DATA, not_1_out);
  and and_2 (and_2_out, Write_EN, Din);
  or or_1 (or_1_out, and_1_out, and_2_out);
  D_Flip_Flop d_ff_1 (.clk(CLK), .D(or_1_out), .Q(Stored_DATA), .reset(RESET));  // open: Qn, preset, en
  assign Dout = OUT_EN ? Stored_DATA : 1'bz;  // Controlled_Buffer controlled_buffer_1
endmodule

module Register (
  input  [7:0] Din,
  input  Write,
  input  CLK,
  input  OUT_EN,
  input  Reset,
  output [7:0] Dout,
  output [7:0] Store
);

  Memory_cell _0 (
    .Write_EN(Din[4]), .Din(Din[4]), .CLK(CLK), .OUT_EN(CLK), .RESET(CLK), .Dout(Dout[0]),
    .Stored_DATA(Store[0]));
  Memory_cell _4 (
    .Din(Din[4]), .CLK(CLK), .OUT_EN(CLK), .RESET(CLK), .Dout(Dout[4]), .Stored_DATA(Store[4]));  // open: Write_EN
  Memory_cell _1 (
    .Write_EN(Din[5]), .Din(Din[5]), .CLK(CLK), .OUT_EN(CLK), .RESET(CLK), .Dout(Dout[1]),
    .Stored_DATA(Store[1]));
  Memory_cell _5 (
    .Din(Din[5]), .CLK(CLK), .OUT_EN(CLK), .RESET(CLK), .Dout(Dout[5]), .Stored_DATA(Store[5]));  // open: Write_EN
  Memory_cell _2 (
    .Write_EN(Din[6]), .Din(Din[6]), .CLK(CLK), .OUT_EN(CLK), .RESET(CLK), .Dout(Dout[2]),
    .Stored_DATA(Store[2]));
  Memory_cell _6 (
    .Din(Din[6]), .CLK(CLK), .OUT_EN(CLK), .RESET(CLK), .Dout(Dout[6]), .Stored_DATA(Store[6]));  // open: Write_EN
  Memory_cell _3 (
    .Write_EN(Din[7]), .Din(Din[7]), .CLK(CLK), .OUT_EN(CLK), .RESET(CLK), .Dout(Dout[3]),
    .Stored_DATA(Store[3]));
  Memory_cell _7 (
    .Din(Din[7]), .CLK(CLK), .OUT_EN(CLK), .RESET(CLK), .Dout(Dout[7]), .Stored_DATA(Store[7]));  // open: Write_EN

  assign OUT_EN = CLK;

  // Notes on the sheet:
  //   8-Bit Register
endmodule

module Half_Adder (
  input  A,
  input  B,
  output SUM,
  output CARRY
);

  and and_1 (CARRY, A, B);
  xor xor_1 (SUM, A, B);
endmodule

module _8BITADDER (
  input  PC0,
  input  PC1,
  input  PC2,
  input  PC3,
  input  PC4,
  input  PC5,
  input  PC6,
  input  PC7,
  output [7:0] PC_PLUS_1
);

  wire half_adder_1_carry, half_adder_2_carry, half_adder_3_carry, half_adder_4_carry, half_adder_5_carry,
       half_adder_6_carry, half_adder_7_carry;

  Half_Adder half_adder_1 (.A(1'b1), .B(PC0), .SUM(PC_PLUS_1[0]), .CARRY(half_adder_1_carry));
  Half_Adder half_adder_2 (.A(half_adder_1_carry), .B(PC1), .SUM(PC_PLUS_1[1]), .CARRY(half_adder_2_carry));
  Half_Adder half_adder_3 (.A(half_adder_2_carry), .B(PC2), .SUM(PC_PLUS_1[2]), .CARRY(half_adder_3_carry));
  Half_Adder half_adder_4 (.A(half_adder_3_carry), .B(PC3), .SUM(PC_PLUS_1[3]), .CARRY(half_adder_4_carry));
  Half_Adder half_adder_5 (.A(half_adder_4_carry), .B(PC4), .SUM(PC_PLUS_1[4]), .CARRY(half_adder_5_carry));
  Half_Adder half_adder_6 (.A(half_adder_5_carry), .B(PC5), .SUM(PC_PLUS_1[5]), .CARRY(half_adder_6_carry));
  Half_Adder half_adder_7 (.A(half_adder_6_carry), .B(PC6), .SUM(PC_PLUS_1[6]), .CARRY(half_adder_7_carry));
  Half_Adder half_adder_8 (.A(half_adder_7_carry), .B(PC7), .SUM(PC_PLUS_1[7]));  // open: CARRY
endmodule

module MUX_2_TO_1_1BIT (
  input  A,
  input  B,
  input  SEL,
  output Y
);

  wire and_1_out, and_2_out, not_1_out;

  not not_1 (not_1_out, SEL);
  and and_1 (and_1_out, A, SEL);
  and and_2 (and_2_out, B, not_1_out);
  or or_1 (Y, and_1_out, and_2_out);
endmodule

module MUX_2_TO_1_8BIT (
  input  [7:0] A,
  input  [7:0] B,
  input  SEL,
  output [7:0] Y
);

  wire not_1_out;

  not not_1 (not_1_out, SEL);
  MUX_2_TO_1_1BIT mux_2_to_1_1bit_1 (.A(A[0]), .B(B[0]), .SEL(not_1_out), .Y(Y[0]));
  MUX_2_TO_1_1BIT mux_2_to_1_1bit_2 (.A(A[1]), .B(B[1]), .SEL(not_1_out), .Y(Y[1]));
  MUX_2_TO_1_1BIT mux_2_to_1_1bit_3 (.A(A[2]), .B(B[2]), .SEL(not_1_out), .Y(Y[2]));
  MUX_2_TO_1_1BIT mux_2_to_1_1bit_4 (.A(A[3]), .B(B[3]), .SEL(not_1_out), .Y(Y[3]));
  MUX_2_TO_1_1BIT mux_2_to_1_1bit_5 (.A(A[4]), .B(B[4]), .SEL(not_1_out), .Y(Y[4]));
  MUX_2_TO_1_1BIT mux_2_to_1_1bit_6 (.A(A[5]), .B(B[5]), .SEL(not_1_out), .Y(Y[5]));
  MUX_2_TO_1_1BIT mux_2_to_1_1bit_7 (.A(A[6]), .B(B[6]), .SEL(not_1_out), .Y(Y[6]));
  MUX_2_TO_1_1BIT mux_2_to_1_1bit_8 (.A(A[7]), .B(B[7]), .SEL(not_1_out), .Y(Y[7]));
endmodule

module Instruction_Splitter (
  input  [15:0] in_1,
  output [3:0] out_2,
  output [3:0] out_3,
  output [3:0] out_4,
  output [3:0] out_5
);


  assign out_2 = in_1[3:0];
  assign out_3 = in_1[7:4];
  assign out_4 = in_1[11:8];
  assign out_5 = in_1[15:12];
endmodule

module Decoder (
  input  in_1,
  input  in_2,
  input  in_3,
  input  in_4
);

  // NOT_Gate not_1 has open pins: in=in_1, out=open
  // NOT_Gate not_2 has open pins: in=in_2, out=open
  // NOT_Gate not_3 has open pins: in=in_3, out=open
  // NOT_Gate not_4 has open pins: in=in_4, out=open
  // AND_Gate and_1 is placed but not wired
  // AND_Gate and_2 is placed but not wired
  // AND_Gate and_3 is placed but not wired
  // AND_Gate and_4 is placed but not wired
  // AND_Gate and_5 is placed but not wired
  // AND_Gate and_6 is placed but not wired
  // AND_Gate and_7 is placed but not wired
  // AND_Gate and_8 is placed but not wired
endmodule

module _1BIT_FULL_ADDER (
  input  A,
  input  B,
  input  Cin,
  output SUM,
  output Cout
);

  wire and_1_out, and_2_out, xor_1_out;

  and and_1 (and_1_out, A, B);
  xor xor_1 (xor_1_out, A, B);
  and and_2 (and_2_out, xor_1_out, Cin);
  xor xor_2 (SUM, xor_1_out, Cin);
  or or_1 (Cout, and_2_out, and_1_out);
endmodule

module _8BIT_FULL_ADDER (
  input  Cin,
  input  [7:0] A,
  input  [7:0] B,
  output [7:0] Y,
  output Cout
);

  wire n1bit_full_adder_1_cout, n1bit_full_adder_2_cout, n1bit_full_adder_3_cout, n1bit_full_adder_4_cout,
       n1bit_full_adder_5_cout, n1bit_full_adder_6_cout, n1bit_full_adder_7_cout;

  _1BIT_FULL_ADDER u_1bit_full_adder_1 (.A(A[0]), .B(B[0]), .Cin(Cin), .SUM(Y[0]), .Cout(n1bit_full_adder_1_cout));
  _1BIT_FULL_ADDER u_1bit_full_adder_2 (
    .A(A[1]), .B(B[1]), .Cin(n1bit_full_adder_1_cout), .SUM(Y[1]), .Cout(n1bit_full_adder_2_cout));
  _1BIT_FULL_ADDER u_1bit_full_adder_3 (
    .A(A[2]), .B(B[2]), .Cin(n1bit_full_adder_2_cout), .SUM(Y[2]), .Cout(n1bit_full_adder_3_cout));
  _1BIT_FULL_ADDER u_1bit_full_adder_4 (
    .A(A[3]), .B(B[3]), .Cin(n1bit_full_adder_3_cout), .SUM(Y[3]), .Cout(n1bit_full_adder_4_cout));
  _1BIT_FULL_ADDER u_1bit_full_adder_5 (
    .A(A[4]), .B(B[4]), .Cin(n1bit_full_adder_4_cout), .SUM(Y[4]), .Cout(n1bit_full_adder_5_cout));
  _1BIT_FULL_ADDER u_1bit_full_adder_6 (
    .A(A[5]), .B(B[5]), .Cin(n1bit_full_adder_5_cout), .SUM(Y[5]), .Cout(n1bit_full_adder_6_cout));
  _1BIT_FULL_ADDER u_1bit_full_adder_7 (
    .A(A[6]), .B(B[6]), .Cin(n1bit_full_adder_6_cout), .SUM(Y[6]), .Cout(n1bit_full_adder_7_cout));
  _1BIT_FULL_ADDER u_1bit_full_adder_8 (.A(A[7]), .B(B[7]), .Cin(n1bit_full_adder_7_cout), .SUM(Y[7]), .Cout(Cout));
endmodule

module _8BIT_SUBRACTOR (
  input  Cin,
  input  [7:0] A,
  input  [7:0] B,
  output [7:0] Y,
  output Bout
);

  wire n1bit_full_adder_1_cout, n1bit_full_adder_2_cout, n1bit_full_adder_3_cout, n1bit_full_adder_4_cout,
       n1bit_full_adder_5_cout, n1bit_full_adder_6_cout, n1bit_full_adder_7_cout, not_1_out, not_2_out,
       not_3_out, not_4_out, not_5_out, not_6_out, not_7_out, not_8_out;

  not not_1 (not_1_out, B[0]);
  not not_2 (not_2_out, B[1]);
  not not_3 (not_3_out, B[2]);
  not not_4 (not_4_out, B[3]);
  not not_5 (not_5_out, B[4]);
  not not_6 (not_6_out, B[5]);
  not not_7 (not_7_out, B[6]);
  not not_8 (not_8_out, B[7]);
  _1BIT_FULL_ADDER u_1bit_full_adder_1 (.A(A[0]), .B(not_1_out), .Cin(Cin), .SUM(Y[0]), .Cout(n1bit_full_adder_1_cout));
  _1BIT_FULL_ADDER u_1bit_full_adder_2 (
    .A(A[1]), .B(not_2_out), .Cin(n1bit_full_adder_1_cout), .SUM(Y[1]), .Cout(n1bit_full_adder_2_cout));
  _1BIT_FULL_ADDER u_1bit_full_adder_3 (
    .A(A[2]), .B(not_3_out), .Cin(n1bit_full_adder_2_cout), .SUM(Y[2]), .Cout(n1bit_full_adder_3_cout));
  _1BIT_FULL_ADDER u_1bit_full_adder_4 (
    .A(A[3]), .B(not_4_out), .Cin(n1bit_full_adder_3_cout), .SUM(Y[3]), .Cout(n1bit_full_adder_4_cout));
  _1BIT_FULL_ADDER u_1bit_full_adder_5 (
    .A(A[4]), .B(not_5_out), .Cin(n1bit_full_adder_4_cout), .SUM(Y[4]), .Cout(n1bit_full_adder_5_cout));
  _1BIT_FULL_ADDER u_1bit_full_adder_6 (
    .A(A[5]), .B(not_6_out), .Cin(n1bit_full_adder_5_cout), .SUM(Y[5]), .Cout(n1bit_full_adder_6_cout));
  _1BIT_FULL_ADDER u_1bit_full_adder_7 (
    .A(A[6]), .B(not_7_out), .Cin(n1bit_full_adder_6_cout), .SUM(Y[6]), .Cout(n1bit_full_adder_7_cout));
  _1BIT_FULL_ADDER u_1bit_full_adder_8 (
    .A(A[7]), .B(not_8_out), .Cin(n1bit_full_adder_7_cout), .SUM(Y[7]), .Cout(Bout));
endmodule

module _8BITADD_SUB (
  input  ADD_SUB,
  input  [7:0] A,
  input  [7:0] B,
  output [7:0] Y,
  output Cout
);

  wire n1bit_full_adder_1_cout, n1bit_full_adder_2_cout, n1bit_full_adder_3_cout, n1bit_full_adder_4_cout,
       n1bit_full_adder_5_cout, n1bit_full_adder_6_cout, n1bit_full_adder_7_cout, xor_1_out, xor_2_out,
       xor_3_out, xor_4_out, xor_5_out, xor_6_out, xor_7_out, xor_8_out;

  xor xor_1 (xor_1_out, B[0], ADD_SUB);
  xor xor_2 (xor_2_out, B[1], ADD_SUB);
  xor xor_3 (xor_3_out, B[2], ADD_SUB);
  xor xor_4 (xor_4_out, B[3], ADD_SUB);
  xor xor_5 (xor_5_out, B[4], ADD_SUB);
  xor xor_6 (xor_6_out, B[5], ADD_SUB);
  xor xor_7 (xor_7_out, B[6], ADD_SUB);
  xor xor_8 (xor_8_out, B[7], ADD_SUB);
  _1BIT_FULL_ADDER u_1bit_full_adder_1 (
    .A(A[0]), .B(xor_1_out), .Cin(ADD_SUB), .SUM(Y[0]), .Cout(n1bit_full_adder_1_cout));
  _1BIT_FULL_ADDER u_1bit_full_adder_2 (
    .A(A[1]), .B(xor_2_out), .Cin(n1bit_full_adder_1_cout), .SUM(Y[1]), .Cout(n1bit_full_adder_2_cout));
  _1BIT_FULL_ADDER u_1bit_full_adder_3 (
    .A(A[2]), .B(xor_3_out), .Cin(n1bit_full_adder_2_cout), .SUM(Y[2]), .Cout(n1bit_full_adder_3_cout));
  _1BIT_FULL_ADDER u_1bit_full_adder_4 (
    .A(A[3]), .B(xor_4_out), .Cin(n1bit_full_adder_3_cout), .SUM(Y[3]), .Cout(n1bit_full_adder_4_cout));
  _1BIT_FULL_ADDER u_1bit_full_adder_5 (
    .A(A[4]), .B(xor_5_out), .Cin(n1bit_full_adder_4_cout), .SUM(Y[4]), .Cout(n1bit_full_adder_5_cout));
  _1BIT_FULL_ADDER u_1bit_full_adder_6 (
    .A(A[5]), .B(xor_6_out), .Cin(n1bit_full_adder_5_cout), .SUM(Y[5]), .Cout(n1bit_full_adder_6_cout));
  _1BIT_FULL_ADDER u_1bit_full_adder_7 (
    .A(A[6]), .B(xor_7_out), .Cin(n1bit_full_adder_6_cout), .SUM(Y[6]), .Cout(n1bit_full_adder_7_cout));
  _1BIT_FULL_ADDER u_1bit_full_adder_8 (
    .A(A[7]), .B(xor_8_out), .Cin(n1bit_full_adder_7_cout), .SUM(Y[7]), .Cout(Cout));
endmodule

module BITWISEAND (
  input  [7:0] A,
  input  [7:0] B,
  output [7:0] Y
);

  and and_1 (Y[0], A[0], B[0]);
  and and_2 (Y[1], A[1], B[1]);
  and and_3 (Y[2], A[2], B[2]);
  and and_4 (Y[3], A[3], B[3]);
  and and_5 (Y[4], A[4], B[4]);
  and and_6 (Y[5], A[5], B[5]);
  and and_7 (Y[6], A[6], B[6]);
  and and_8 (Y[7], A[7], B[7]);
endmodule

module BITWISENOR (
  input  [7:0] A,
  input  [7:0] B,
  output [7:0] Y
);

  nor nor_1 (Y[0], A[0], B[0]);
  nor nor_2 (Y[1], A[1], B[1]);
  nor nor_3 (Y[2], A[2], B[2]);
  nor nor_4 (Y[3], A[3], B[3]);
  nor nor_5 (Y[4], A[4], B[4]);
  nor nor_6 (Y[5], A[5], B[5]);
  nor nor_7 (Y[6], A[6], B[6]);
  nor nor_8 (Y[7], A[7], B[7]);
endmodule

module ALUDECODER (
  input  [3:0] OPCODE,
  output ADD,
  output SUB,
  output NOR,
  output AND,
  output INC,
  output DEC,
  output RSH
);

  wire not_1_out, not_2_out, not_3_out, not_4_out;

  not not_1 (not_1_out, OPCODE[0]);
  not not_2 (not_2_out, OPCODE[1]);
  not not_3 (not_3_out, OPCODE[2]);
  not not_4 (not_4_out, OPCODE[3]);
  Bit_Extender #(.in_width(1), .out_width(8), .\type ("one")) bit_extender_1 ();  // open: in, out
  Bit_Extender #(.in_width(1), .out_width(8), .\type ("one")) bit_extender_2 ();  // open: in, out
  Bit_Extender #(.in_width(1), .out_width(8), .\type ("one")) bit_extender_3 ();  // open: in, out
  Bit_Extender #(.in_width(1), .out_width(8), .\type ("one")) bit_extender_4 ();  // open: in, out
  Bit_Extender #(.in_width(1), .out_width(8), .\type ("one")) bit_extender_5 ();  // open: in, out
  Bit_Extender #(.in_width(1), .out_width(8), .\type ("one")) bit_extender_6 ();  // open: in, out
  Bit_Extender #(.in_width(1), .out_width(8), .\type ("one")) bit_extender_7 ();  // open: in, out
  and and_1 (ADD, not_1_out, OPCODE[1], not_3_out, not_4_out);
  and and_2 (SUB, OPCODE[0], OPCODE[1], not_3_out, not_4_out);
  and and_3 (NOR, OPCODE[0], not_2_out, OPCODE[2], not_4_out);
  and and_4 (AND, not_1_out, OPCODE[1], OPCODE[2], not_4_out);
  and and_5 (INC, not_1_out, not_2_out, not_3_out, OPCODE[3]);
  and and_6 (DEC, OPCODE[0], not_2_out, not_3_out, OPCODE[3]);
  and and_7 (RSH, not_1_out, OPCODE[1], not_3_out, OPCODE[3]);
endmodule

module RIGHTSHIFT (
  input  [7:0] IN,
  input  in_2,
  output RSHCARRY,
  output [7:0] RSH
);


  assign RSH = {in_2, IN[7:1]};
  assign RSHCARRY = IN[0];
endmodule

module ALU_2 (
  input  [7:0] A,
  input  [7:0] B,
  input  [3:0] OPCODE,
  output ZERO,
  output CARRY,
  output NEGATIVE,
  output FALL_OFF,
  output [7:0] out_8,
  output [7:0] out_9,
  output [7:0] out_10
);

  wire aludecoder_1_dec, aludecoder_1_inc, aludecoder_1_sub, or_1_out, or_2_out;
  wire [7:0] bitwiseand_1_y, bitwisenor_1_y, rightshift_1_rsh;

  ALUDECODER aludecoder_1 (
    .OPCODE(OPCODE), .SUB(aludecoder_1_sub), .INC(aludecoder_1_inc), .DEC(aludecoder_1_dec));  // open: ADD, NOR, AND, RSH
  or or_1 (or_1_out, aludecoder_1_inc, aludecoder_1_dec);
  or or_2 (or_2_out, aludecoder_1_sub, aludecoder_1_dec);
  MUX_2_TO_1_8BIT mux_2_to_1_8bit_1 (.A(B), .SEL(or_1_out), .B(8'h1), .Y(A));
  _8BITADD_SUB u_8bitadd_sub_1 (.ADD_SUB(or_2_out), .A(A), .B(A), .Y({NEGATIVE, out_10[6:0]}), .Cout(CARRY));
  BITWISENOR bitwisenor_1 (.A(A), .B(B), .Y(bitwisenor_1_y));
  BITWISEAND bitwiseand_1 (.A(A), .B(B), .Y(bitwiseand_1_y));
  RIGHTSHIFT rightshift_1 (.IN(A), .RSHCARRY(FALL_OFF), .RSH(rightshift_1_rsh));  // open: in_2
  nand nand_1 (ZERO, out_10[0], out_10[1], out_10[2], out_10[3], out_10[4], out_10[5], out_10[6], NEGATIVE);
  Multiplexer #(.select(4), .width(8)) multiplexer_1 (
    .in2({NEGATIVE, out_10[6:0]}), .in3({NEGATIVE, out_10[6:0]}), .in4(bitwisenor_1_y), .in5(bitwiseand_1_y),
    .in6({NEGATIVE, out_10[6:0]}), .in7({NEGATIVE, out_10[6:0]}), .in8(rightshift_1_rsh), .out(out_8),
    .sel(OPCODE), .en(1'b1));  // open: in0, in1, in9, in10, in11, in12, in13, in14, in15

  assign out_9 = A;
  assign out_10[7] = NEGATIVE;
endmodule

module _16_1_MUX (
);

  MUX_2_TO_1_8BIT mux_2_to_1_8bit_1 ();  // open: A, SEL, B, Y
  MUX_2_TO_1_8BIT mux_2_to_1_8bit_2 ();  // open: A, SEL, B, Y
  MUX_2_TO_1_8BIT mux_2_to_1_8bit_3 ();  // open: A, SEL, B, Y
  MUX_2_TO_1_8BIT mux_2_to_1_8bit_4 ();  // open: A, SEL, B, Y
  MUX_2_TO_1_8BIT mux_2_to_1_8bit_5 ();  // open: A, SEL, B, Y
  MUX_2_TO_1_8BIT mux_2_to_1_8bit_6 ();  // open: A, SEL, B, Y
  MUX_2_TO_1_8BIT mux_2_to_1_8bit_7 ();  // open: A, SEL, B, Y
  MUX_2_TO_1_8BIT mux_2_to_1_8bit_8 ();  // open: A, SEL, B, Y
endmodule
